// Logisim project ula.circ as structural Verilog: 3 circuits, main circuit main
module main (
  input  [4:0] A,
  input  [4:0] B,
  input  [3:0] Seletor,
  output Flag_Carry,
  output Flag_o,
  output [4:0] Resultado
);

  wire [4:0] bloco_aritmetico_1_inc_a, bloco_aritmetico_1_inc_b, bloco_aritmetico_1_soma,
       bloco_aritmetico_1_subtrator, bloco_logico_1_out_and, bloco_logico_1_out_nota,
       bloco_logico_1_out_notb, bloco_logico_1_out_or, bloco_logico_1_out_xor;

  Bloco_aritmetico bloco_aritmetico_1 (
    .A(A), .B(B), .Soma(bloco_aritmetico_1_soma), .Subtrator(bloco_aritmetico_1_subtrator),
    .Inc_A(bloco_aritmetico_1_inc_a), .Inc_B(bloco_aritmetico_1_inc_b), .Carry_out(Flag_Carry));
  Bloco_logico bloco_logico_1 (
    .A(A), .B(B), .Out_AND(bloco_logico_1_out_and), .Out_OR(bloco_logico_1_out_or),
    .Out_XOR(bloco_logico_1_out_xor), .Out_NOTA(bloco_logico_1_out_nota), .Out_NoTB(bloco_logico_1_out_notb));
  Multiplexer #(.select(4), .width(5)) multiplexer_1 (
    .in0(bloco_aritmetico_1_soma), .in1(bloco_aritmetico_1_subtrator), .in2(bloco_aritmetico_1_inc_a),
    .in3(bloco_aritmetico_1_inc_b), .in4(bloco_logico_1_out_and), .in5(bloco_logico_1_out_or),
    .in6(bloco_logico_1_out_xor), .in7(bloco_logico_1_out_nota), .in8(bloco_logico_1_out_notb),
    .out(Resultado), .sel(Seletor));  // open: in9, in10, in11, in12, in13, in14, in15, en
  nor nor_1 (Flag_o, Resultado[0], Resultado[1], Resultado[2], Resultado[3], Resultado[4]);
  // Probe on Resultado
endmodule

module Bloco_aritmetico (
  input  [4:0] A,
  input  [4:0] B,
  output [4:0] Soma,
  output [4:0] Subtrator,
  output [4:0] Inc_A,
  output [4:0] Inc_B,
  output Carry_out
);

  Adder #(.width(5)) adder_1 (.a(A), .b(B), .out(Soma), .cout(Carry_out));  // open: cin
  Subtractor #(.width(5)) subtractor_1 (.a(A), .b(B), .out(Subtrator));  // open: bin, bout
  Adder #(.width(5)) adder_2 (.a(A), .b(5'b00001), .out(Inc_A));  // open: cin, cout
  Adder #(.width(5)) adder_3 (.a(B), .b(5'b00001), .out(Inc_B));  // open: cin, cout
endmodule

module Bloco_logico (
  input  [4:0] A,
  input  [4:0] B,
  output [4:0] Out_AND,
  output [4:0] Out_OR,
  output [4:0] Out_XOR,
  output [4:0] Out_NOTA,
  output [4:0] Out_NoTB
);

  assign Out_NOTA = ~A;  // NOT_Gate not_1, 5 bits wide
  assign Out_NoTB = ~B;  // NOT_Gate not_2, 5 bits wide
  assign Out_AND = A & B;  // AND_Gate and_1, 5 bits wide
  assign Out_OR = A | B;  // OR_Gate or_1, 5 bits wide
  assign Out_XOR = A ^ B;  // XOR_Gate xor_1, 5 bits wide
endmodule
